# Fritzing sketch schematic (saved by Fritzing 0.9.2b)
breadboards: 1

parts:
  LED_Driver_1 = DC Power [voltage=24V part_number="200W - 8.6A"]
  LED_1 = LED - 5mm [color="Red (633nm)" current=2.5A part_number="25 meters" package="5 mm [THT]"]
  LED_2 = LED - 5mm [color="Red (633nm)" current=2.5A part_number="25 meters" package="5 mm [THT]"]
  Q2 = Basic FET N-Channel [part_number=STP16NF06L package="D2Pak [SMD]"]
  Q1 = Basic FET N-Channel [part_number=STP16NF06L package="D2Pak [SMD]"]
  LED_Driver_2 = DC Power [voltage=24V part_number="200W - 8.6A"]
  LED_3 = LED - 5mm [color="Red (633nm)" current=2.5A part_number="25 meters" package="5 mm [THT]"]
  LED_4 = LED - 5mm [color="Red (633nm)" current=2.5A part_number="25 meters" package="5 mm [THT]"]
  Q3 = Basic FET N-Channel [part_number=STP16NF06L package="D2Pak [SMD]"]
  Q4 = Basic FET N-Channel [part_number=STP16NF06L package="D2Pak [SMD]"]
  LED_Driver_3 = DC Power [voltage=24V part_number="200W - 8.6A"]
  LED_5 = LED - 5mm [color="Red (633nm)" current=2.5A part_number="25 meters" package="5 mm [THT]"]
  LED_6 = LED - 5mm [color="Red (633nm)" current=2.5A part_number="25 meters" package="5 mm [THT]"]
  Q5 = Basic FET N-Channel [part_number=STP16NF06L package="D2Pak [SMD]"]
  Q6 = Basic FET N-Channel [part_number=STP16NF06L package="D2Pak [SMD]"]
  LED_Driver_4 = DC Power [voltage=24V part_number="200W - 8.6A"]
  LED_Driver_5 = DC Power [voltage=24V part_number="200W - 8.6A"]
  LED_Driver_6 = DC Power [voltage=24V part_number="200W - 8.6A"]
  LED_7 = LED - 5mm [color="Red (633nm)" current=2.5A part_number="25 meters" package="5 mm [THT]"]
  LED_9 = LED - 5mm [color="Red (633nm)" current=2.5A part_number="25 meters" package="5 mm [THT]"]
  LED_11 = LED - 5mm [color="Red (633nm)" current=2.5A part_number="25 meters" package="5 mm [THT]"]
  LED_8 = LED - 5mm [color="Red (633nm)" current=2.5A part_number="25 meters" package="5 mm [THT]"]
  LED_12 = LED - 5mm [color="Red (633nm)" current=2.5A part_number="25 meters" package="5 mm [THT]"]
  LED_10 = LED - 5mm [color="Red (633nm)" current=2.5A part_number="25 meters" package="5 mm [THT]"]
  Q7 = Basic FET N-Channel [part_number=STP16NF06L package="D2Pak [SMD]"]
  Q10 = Basic FET N-Channel [part_number=STP16NF06L package="D2Pak [SMD]"]
  Q8 = Basic FET N-Channel [part_number=STP16NF06L package="D2Pak [SMD]"]
  Q11 = Basic FET N-Channel [part_number=STP16NF06L package="D2Pak [SMD]"]
  Q9 = Basic FET N-Channel [part_number=STP16NF06L package="D2Pak [SMD]"]
  Q12 = Basic FET N-Channel [part_number=STP16NF06L package="D2Pak [SMD]"]
  mc = Arduino Uno (Rev3)
  BCI_Pulse_Oximeter = mystery part, 2 pins [chip_label=BCI]

nets:
  N1: LED_Driver_1.V+, LED_1.anode, LED_2.anode
  N2: LED_Driver_1.V-, Q2.source, Q1.source, LED_Driver_4.V-, LED_Driver_5.V-, LED_Driver_6.V-, Q7.source, Q10.source, Q8.source, Q11.source, Q9.source, Q12.source, mc.GND, BCI_Pulse_Oximeter.pin1
  N3: LED_1.cathode, Q1.drain
  N4: LED_2.cathode, Q2.drain
  N5: Q2.Gate, Q1.Gate, Q3.Gate, Q4.Gate, Q5.Gate, Q6.Gate, mc.D10_PWM/SS
  N6: LED_Driver_2.V+, LED_3.anode, LED_4.anode
  N7: LED_Driver_2.V-, Q3.source, Q4.source
  N8: LED_3.cathode, Q3.drain
  N9: LED_4.cathode, Q4.drain
  N10: LED_Driver_3.V+, LED_5.anode, LED_6.anode
  N11: LED_Driver_3.V-, Q5.source, Q6.source
  N12: LED_5.cathode, Q5.drain
  N13: LED_6.cathode, Q6.drain
  N14: LED_Driver_4.V+, LED_7.anode, LED_8.anode
  N15: LED_Driver_5.V+, LED_9.anode, LED_10.anode
  N16: LED_Driver_6.V+, LED_11.anode, LED_12.anode
  N17: LED_7.cathode, Q7.drain
  N18: LED_9.cathode, Q9.drain
  N19: LED_11.cathode, Q11.drain
  N20: LED_8.cathode, Q8.drain
  N21: LED_12.cathode, Q12.drain
  N22: LED_10.cathode, Q10.drain
  N23: Q7.Gate, Q10.Gate, Q8.Gate, Q11.Gate, Q9.Gate, Q12.Gate, mc.D9_PWM
  N24: mc.D13/SCK, BCI_Pulse_Oximeter.pin2

notes:
  Heart Of The City
  Heart of The City, Circuit design by Aravinth Panchadcharam, 2.0
  LED Fade Signal
  LED Blink Signal
